# Fritzing sketch led_control (saved by Fritzing 0.9.1b)

parts:
  Raspberry_Pi1 = Raspberry Pi B+
  LED2 = LED - 5mm [color="Blue (505nm)" package="5 mm [THT]"]

nets:
  N1: Raspberry_Pi1.GPIO14, LED2.anode
  N2: Raspberry_Pi1.GND, LED2.cathode
