# Fritzing sketch motors_wiring (saved by Fritzing 0.9.2b)

parts:
  Raspberry_Pi_HAT1 = ACROBOTIC HAT Motor [part_number=RPI-00015]
  Motor2 = ACROBOTIC Micro Gearmotor w/ Encoder
  Motor3 = ACROBOTIC Micro Gearmotor w/ Encoder

nets:
  N1: Raspberry_Pi_HAT1.MOTA+, Motor2.MPOS
  N2: Raspberry_Pi_HAT1.MOTA-, Motor2.MNEG
  N3: Raspberry_Pi_HAT1.3V3#connectorMota3, Motor2.VCC
  N4: Raspberry_Pi_HAT1.ENCB2#connectorMota4, Motor2.ENC2
  N5: Raspberry_Pi_HAT1.ENCB1#connectorMota5, Motor2.ENC1
  N6: Raspberry_Pi_HAT1.GND#connectorMota6, Motor2.GND
  N7: Raspberry_Pi_HAT1.MOTB+, Motor3.MPOS
  N8: Raspberry_Pi_HAT1.MOTB-, Motor3.MNEG
  N9: Raspberry_Pi_HAT1.3V3#connectorMotb3, Motor3.VCC
  N10: Raspberry_Pi_HAT1.ENCB2#connectorMotb4, Motor3.ENC2
  N11: Raspberry_Pi_HAT1.ENCB1#connectorMotb5, Motor3.ENC1
  N12: Raspberry_Pi_HAT1.GND#connectorMotb6, Motor3.GND

custom parts:
  ACROBOTIC HAT Motor: Control DC, Stepper, and Servo Motors from your Rasbperry Pi!
