# Fritzing sketch motor_control_direct2 (saved by Fritzing 0.9.1b)

parts:
  Raspberry_Pi1 = Raspberry Pi B+
  M1 = DC Motor

nets:
  N1: Raspberry_Pi1.GPIO14, M1.pin_2
  N2: Raspberry_Pi1.GND, M1.pin_1
