# Fritzing sketch motor_wiring (saved by Fritzing 0.9.2b)

parts:
  Raspberry_Pi_HAT1 = ACROBOTIC HAT Motor [part_number=RPI-00015]
  Motor2 = ACROBOTIC Micro Gearmotor w/ Encoder

nets:
  N1: Raspberry_Pi_HAT1.MOTA+, Motor2.MPOS
  N2: Raspberry_Pi_HAT1.MOTA-, Motor2.MNEG
  3V3: Raspberry_Pi_HAT1.3V3, Motor2.VCC
  N3: Raspberry_Pi_HAT1.ENCB2, Motor2.ENC2
  N4: Raspberry_Pi_HAT1.ENCB1, Motor2.ENC1
  GND: Raspberry_Pi_HAT1.GND, Motor2.GND

custom parts:
  ACROBOTIC HAT Motor: Control DC, Stepper, and Servo Motors from your Rasbperry Pi!
