# Fritzing sketch activity2 (saved by Fritzing 0.9.2b)

parts:
  Raspberry_Pi_HAT1 = ACROBOTIC HAT Motor [part_number=RPI-00015]
  Motor1 = ACROBOTIC Line Sensor_1

nets:
  GND: Raspberry_Pi_HAT1.GND, Motor1.GND
  3V3: Raspberry_Pi_HAT1.3V3, Motor1.VCC
  N1: Raspberry_Pi_HAT1.AIN00, Motor1.LDR

custom parts:
  ACROBOTIC HAT Motor: Control DC, Stepper, and Servo Motors from your Rasbperry Pi!
  ACROBOTIC Line Sensor_1: ACROBOTIC Micro Gearmotor w/ Encoder
