# Fritzing sketch main (saved by Fritzing 0.9.2b)

parts:
  Raspberry_Pi_HAT1 = ACROBOTIC HAT Motor [part_number=RPI-00015]
  Motor1 = ACROBOTIC Line Sensor_1
  Part1 = HC-SR04

nets:
  N1: Raspberry_Pi_HAT1.GND#connectorAin1, Motor1.GND
  3V3: Raspberry_Pi_HAT1.3V3, Motor1.VCC
  N2: Raspberry_Pi_HAT1.AIN03, Motor1.L
  N3: Raspberry_Pi_HAT1.AIN02, Motor1.C
  N4: Raspberry_Pi_HAT1.AIN01, Motor1.R
  N5: Raspberry_Pi_HAT1.AIN00, Motor1.LDR
  N6: Raspberry_Pi_HAT1.GND#connectorUltrasonic1, Part1.Gnd
  N7: Raspberry_Pi_HAT1.GPIO6, Part1.Trig
  N8: Raspberry_Pi_HAT1.GPIO5, Part1.Echo
  5V: Raspberry_Pi_HAT1.5V, Part1.Vcc

custom parts:
  ACROBOTIC HAT Motor: Control DC, Stepper, and Servo Motors from your Rasbperry Pi!
  ACROBOTIC Line Sensor_1: ACROBOTIC Micro Gearmotor w/ Encoder
  HC-SR04: HC-SR04 ultrasonic distance sensor
