# Fritzing sketch activity1 (saved by Fritzing 0.9.2b)

parts:
  Raspberry_Pi_HAT1 = ACROBOTIC HAT Motor [part_number=RPI-00015]
  Part1 = HC-SR04

nets:
  GND: Raspberry_Pi_HAT1.GND, Part1.Gnd
  N1: Raspberry_Pi_HAT1.GPIO6, Part1.Echo
  N2: Raspberry_Pi_HAT1.GPIO5, Part1.Trig
  5V: Raspberry_Pi_HAT1.5V, Part1.Vcc

custom parts:
  ACROBOTIC HAT Motor: Control DC, Stepper, and Servo Motors from your Rasbperry Pi!
  HC-SR04: HC-SR04 ultrasonic distance sensor
